# Fritzing sketch board (saved by Fritzing 0.9.3b)
breadboards: 2

parts:
  S1 = Pushbutton [package="[THT]"]
  S2 = Pushbutton [package="[SMD]"]
  Part1 = Arduino Nano (Rev3.0) (ICSP)
  Squix1 = OLED 0.96" 128x64 I2C SSD1306
  Q1 = Basic FET N-Channel [package="TO220 [THT]"]
  R1 = Resistor [tolerance=±0.5% resistance=100 package=THT]
  R2 = Resistor [tolerance=±5% resistance=100 package=THT]
  R3 = Resistor [tolerance=±5% resistance=100 package=THT]
  J1 = Screw terminal - 2 pins [package=THT]
  R4 = Resistor [tolerance=±5% resistance=100 package=THT]
  S3 = Toggle Switch [package=THT]
  LED1 = LED - 3mm [color="Red (633nm)" package="3 mm [THT]"]
  LED3 = LED - 3mm [color="Red (633nm)" package="3 mm [THT]"]
  LED2 = LED - 3mm [color="Red (633nm)" package="3 mm [THT]"]
  Pololu_A1 = Pololu A4988 [package=SO16]
  R5 = Resistor [tolerance=±5% resistance=560 package=THT]
  R6 = Resistor [tolerance=±5% resistance=560 package=THT]
  R7 = Resistor [tolerance=±5% resistance=560 package=THT]
  S4 = Pushbutton [package="[THT]"]
  R8 = Resistor [tolerance=±5% resistance=100 package=THT]
  M1 = Stepper Motor - Bipolar
  C1 = Electrolytic Capacitor [capacitance=100nF voltage=20V package="100 mil [THT, electrolytic]"]
  LED4 = LED - 3mm [color="Red (633nm)" package="3 mm [THT]"]
  LED5 = LED - 3mm [color="Red (633nm)" package="3 mm [THT]"]
  R9 = Resistor [tolerance=±5% resistance=560 package=THT]
  R10 = Resistor [tolerance=±5% resistance=560 package=THT]
  J2 = Piezo Speaker

nets:
  N1: S1.Pin_1, S1.Pin_2, Part1.D11/MOSI, R3.Pin_1
  5V: S1.Pin_3, S1.Pin_4, S2.Pin_3, S2.Pin_4, Part1.5V, Squix1.VCC, S3.COM, Pololu_A1.VDD, S4.Pin_3, S4.Pin_4, LED4.cathode, LED5.cathode
  N2: S2.Pin_1, S2.Pin_2, Part1.D13/SCK, R4.Pin_1
  GND: Part1.GND, Squix1.GND, Q1.source, R1.Pin_0, R2.Pin_0, R3.Pin_0, J1.pin1, R4.Pin_0, LED1.cathode, LED3.cathode, LED2.cathode, Pololu_A1.GND, R8.Pin_0, C1.-, J2.pin1
  N3: Part1.D2, Pololu_A1.DIR
  N4: Part1.D3, Pololu_A1.STEP
  N5: Part1.D4, R9.Pin_1
  N6: Part1.D5, R10.Pin_1
  N7: Part1.D6, S4.Pin_1, S4.Pin_2, R8.Pin_1
  N8: Part1.D9, Q1.gate, R1.Pin_1
  N9: Part1.D10, R2.Pin_1, S3.L2
  N10: Part1.D12/MISO, J2.pin2
  N11: Part1.A5, Squix1.SCL
  N12: Part1.A4, Squix1.SCA
  N13: Part1.A3, Pololu_A1.ENABLE
  N14: Part1.A2, R6.Pin_1
  N15: Part1.A1, R7.Pin_1
  N16: Part1.A0, R5.Pin_1
  N17: J1.pin2, Pololu_A1.VMOT, C1.+
  N18: LED1.anode, R6.Pin_0
  N19: LED3.anode, R5.Pin_0
  N20: LED2.anode, R7.Pin_0
  N21: Pololu_A1.1B, M1.A
  N22: Pololu_A1.1A, M1.C
  N23: Pololu_A1.2A, M1.B
  N24: Pololu_A1.2B, M1.D
  N25: LED4.anode, R10.Pin_0
  N26: LED5.anode, R9.Pin_0
